# Fritzing sketch MontagemBluetooth (saved by Fritzing 0.8.5b)
breadboards: 1

parts:
  R1 = Resistor [tolerance=±5% resistance=220 package=THT]
  R2 = Resistor [tolerance=±5% resistance=220 package=THT]
  LED3 = LED - 5mm [color="Red (633nm)" package="5 mm [THT]"]
  LED4 = LED - 5mm [color="Green (555nm)" package="5 mm [THT]"]
  Part1 = Arduino Uno (Rev3)
  Part3 = Bluetooth HC-06

nets:
  GND: R1.Pin_0, R2.Pin_0, Part1.GND, Part3.GND
  N1: R1.Pin_1, LED3.cathode
  N2: R2.Pin_1, LED4.cathode
  N3: LED3.anode, Part1.D5_PWM
  N4: LED4.anode, Part1.D6_PWM
  N5: Part1.D0/RX, Part3.TXD
  N6: Part1.D1/TX, Part3.RXD
  5V: Part1.5V, Part3.VCC
